# Fritzing sketch Prototype_01 (saved by Fritzing 0.8.7b)
circuit board: 8.46667cm x 5.64444cm
breadboards: 1

parts:
  R1 = Resistor [tolerance=±5% resistance=220 package=THT]
  R2_Photoresistor = Photocell (LDR) [package=THT]
  Part1 = Arduino Uno (Rev3)
  R3 = Resistor [tolerance=±5% resistance=10k package=THT]
  U1_Potentiometer = POT [package=alps_pot]
  LED1 = LEDs [package=led10mm]
  U2 = LCD-16X2 [package=lcd-8x2]
  R4 = Resistor [tolerance=±5% resistance=3.3k package=THT]
  S1_Button = Pushbutton [package="[THT]"]
  R5 = Resistor [tolerance=±5% resistance=10k package=THT]

nets:
  GND: R1.Pin_0, Part1.GND, R3.Pin_1, U1_Potentiometer.A, U2.VSS, U2.R_W, U2.K, R4.Pin_1, S1_Button.Pin_3, S1_Button.Pin_4
  N1: R1.Pin_1, LED1.A
  5V: R2_Photoresistor.pin_0, Part1.5V, U1_Potentiometer.E, U2.VDD, U2.A, R5.Pin_1
  N2: R2_Photoresistor.pin_1, Part1.A0, R3.Pin_0
  N3: Part1.A1, U1_Potentiometer.S
  N4: Part1.A2, S1_Button.Pin_1, R5.Pin_0
  N5: Part1.D9_PWM, LED1.C
  N6: Part1.D11_PWM/MOSI, U2.E
  N7: Part1.D12/MISO, U2.RS
  N8: Part1.D2, U2.DB7
  N9: Part1.D3_PWM, U2.DB6
  N10: Part1.D4, U2.DB5
  N11: Part1.D5_PWM, U2.DB4
  N12: U2.VO, R4.Pin_0
